// Logisim project Four_Bits_Add_Sub.circ as structural Verilog: 2 circuits, main circuit Add_Sub_4Bits
module Add_Sub_4Bits (
  input  [3:0] A,
  input  [3:0] B,
  input  Add_Sub,
  output [3:0] R,
  output Zero,
  output Overflow
);

  wire add_1bit_1_cout, add_1bit_2_cout, add_1bit_3_cout, add_1bit_4_cout, not_1_out, xor_1_out, xor_2_out,
       xor_3_out, xor_4_out;

  // Probe on A
  Add_1Bit add_1bit_1 (.A(A[3]), .Cout(add_1bit_1_cout), .B(xor_1_out), .Sum(R[3]), .Cin(add_1bit_2_cout));
  xor xor_1 (xor_1_out, B[3], not_1_out);
  // Probe on B
  xor xor_2 (xor_2_out, B[2], not_1_out);
  Add_1Bit add_1bit_2 (.A(A[2]), .Cout(add_1bit_2_cout), .B(xor_2_out), .Sum(R[2]), .Cin(add_1bit_3_cout));
  xor xor_3 (xor_3_out, B[1], not_1_out);
  xor xor_4 (xor_4_out, B[0], not_1_out);
  Add_1Bit add_1bit_3 (.A(A[1]), .Cout(add_1bit_3_cout), .B(xor_3_out), .Sum(R[1]), .Cin(add_1bit_4_cout));
  xor xor_5 (Overflow, add_1bit_2_cout, add_1bit_1_cout);
  not not_1 (not_1_out, Add_Sub);
  Add_1Bit add_1bit_4 (.A(A[0]), .Cout(add_1bit_4_cout), .B(xor_4_out), .Sum(R[0]), .Cin(not_1_out));
  // Probe on R
  nor nor_1 (Zero, R[0], R[1], R[2], R[3]);

  // Notes on the sheet:
  //   Leila Erbay 260672158
  //   MAKE SURE THAT YOU OPENED THIS PROJECT IN "LOGISIM-EVOLUTION"
  //   YOU CAN FIND "LOGISIM-EVOLUTION" PROGRAM IN THE ASSIGNMENT'S FOLDER
  //   DO NOT USE "LOGISIM" VERSION TO SOLVE THIS ASSIGNMENT!
endmodule

module Add_1Bit (
  input  Cin,
  input  A,
  input  B,
  output Sum,
  output Cout
);

  wire and_1_out, and_2_out, xor_1_out, xor_2_out;

  xor xor_1 (xor_1_out, Cin, B);
  xor xor_2 (xor_2_out, A, B);
  xor xor_3 (Sum, xor_1_out, A);
  and and_1 (and_1_out, A, B);
  and and_2 (and_2_out, Cin, xor_2_out);
  or or_1 (Cout, and_1_out, and_2_out);

  // Notes on the sheet:
  //   Leila Erbay   260672158
  //   MAKE SURE THAT YOU OPENED THIS PROJECT IN "LOGISIM-EVOLUTION"
  //   YOU CAN FIND "LOGISIM-EVOLUTION" PROGRAM IN THE ASSIGNMENT'S FOLDER
  //   DO NOT USE "LOGISIM" VERSION TO SOLVE THIS ASSIGNMENT!
endmodule
